# Fritzing sketch ForceSensorWithLED (saved by Fritzing 0.9.5d)
breadboards: 1

parts:
  J1 = Basic Force Sensing Resistor (FSR) [package=THT]
  Part1 = Arduino Uno (Rev3)
  R1 = Resistor [tolerance=±5% resistance=10 package=THT]
  LED1 = LED - 5mm [color="Red (633nm)" package="5 mm [THT]"]
  R2 = Resistor [tolerance=±5% resistance=220 package=THT]

nets:
  N1: J1.pin_0, Part1.5V, R1.Pin_0
  N2: J1.pin_1, Part1.A0, R1.Pin_1
  N3: Part1.D13/SCK, R2.Pin_1
  N4: Part1.GND, LED1.anode
  N5: LED1.cathode, R2.Pin_0
